# Fritzing sketch Cheapspark (saved by Fritzing 0.9.2b)
circuit board: 6cm x 3cm
breadboards: 1

parts:
  R1 = Resistor [tolerance=±5% resistance=470 package=THT]
  R2 = Resistor [tolerance=±5% resistance=220 package=THT]
  Vin = female pin header, 2 pins [form="♀ (female)"]
  SW3 = Momentary Switch [package=ksa_sealed_tac_switch]
  SW1 = Momentary Switch [package=ksa_sealed_tac_switch]
  SW0 = Momentary Switch [package=ksa_sealed_tac_switch]
  Part1 = Arduino Nano (Rev3.0)
  5v = mystery part, 3 pins [chip_label=?]
  GND = mystery part, 3 pins [chip_label=?]
  Vout = female pin header, 2 pins [form="♀ (female)"]
  R3 = Resistor [tolerance=±5% resistance=220 package=THT]
  1W = female pin header, 3 pins [form="♀ (female)"]
  DHT22 = female pin header, 4 pins [form="♀ (female)"]
  R4 = Resistor [tolerance=±5% resistance=220 package=THT]
  J1 = female pin header, 15 pins [form="♀ (female)"]
  5v_2 = female pin header, 2 pins [form="♀ (female)"]
  3_3v = mystery part, 3 pins [chip_label=?]
  GND_2 = female pin header, 2 pins [form="♀ (female)"]
  J2 = female pin header, 15 pins [form="♀ (female)"]
  J3 = male pin header, 2 pins [form="♂ (male)"]
  ESP = double row male pin header, 8 pins [form="♂ (male)"]
  SW2 = Momentary Switch [package=ksa_sealed_tac_switch]

nets:
  N1: R1.Pin_0, Vin.pin2, SW3.2, Part1.GND, GND.pin1, GND.pin2, GND.pin3, 1W.pin1, J1.pin2, GND_2.pin1, GND_2.pin2, J2.pin4, ESP.pin8, SW2.1
  N2: R1.Pin_1, R2.Pin_0, ESP.pin5
  N3: R2.Pin_1, Part1.D1/TX, J2.pin1
  N4: Vin.pin1, Part1.5V, 5v.pin1, 5v.pin2, 5v.pin3, R3.Pin_0, 1W.pin3, J1.pin4, 5v_2.pin1, 5v_2.pin2, J3.pin1
  N5: SW3.1, SW1.2
  N6: SW3.3, Part1.A3, J1.pin9
  N7: SW1.1, SW0.2, DHT22.pin3, DHT22.pin4
  N8: SW1.3, Part1.A1, J1.pin11
  N9: SW0.4, Part1.A0, J1.pin12
  N10: Part1.D0/RX, J2.pin2, ESP.pin1
  N11: Part1.RESET, J1.pin3, J2.pin3, ESP.pin7
  N12: Part1.D2, R3.Pin_1, 1W.pin2, J2.pin5
  N13: Part1.D3, J2.pin6
  N14: Part1.D4, J2.pin7
  N15: Part1.D5, J2.pin8
  N16: Part1.D6, J2.pin9
  N17: Part1.D7, J2.pin10
  N18: Part1.D8, DHT22.pin2, R4.Pin_0, J2.pin11
  N19: Part1.D9, J2.pin12
  N20: Part1.D10, J2.pin13
  N21: Part1.D11/MOSI, J2.pin14
  N22: Part1.D12/MISO, J2.pin15
  N23: Part1.VIN, J1.pin1
  N24: Part1.A7, J1.pin5
  N25: Part1.A6, J1.pin6
  N26: Part1.A5, J1.pin7
  N27: Part1.A4, J1.pin8
  N28: Part1.A2, J1.pin10, SW2.3
  N29: Part1.AREF, J1.pin13
  N30: Part1.3V3, J1.pin14
  N31: Part1.D13/SCK, J1.pin15
  N32: Vout.pin1, 3_3v.pin1, 3_3v.pin2, 3_3v.pin3, ESP.pin2, ESP.pin4
  N33: DHT22.pin1, R4.Pin_1, J3.pin2

notes:
  CHEAPSPARK 5.0
