# Fritzing sketch CheapsparkS (saved by Fritzing 0.9.2b)
circuit board: 6cm x 3cm
breadboards: 1

parts:
  R1 = Resistor [tolerance=±5% resistance=470 package=THT]
  R2 = Resistor [tolerance=±5% resistance=220 package=THT]
  Vin = female pin header, 2 pins [form="♀ (female)"]
  S3 = Momentary Switch [package=ksa_sealed_tac_switch]
  S2 = Momentary Switch [package=ksa_sealed_tac_switch]
  B = mystery part, 15 pins [chip_label=?]
  S1 = Momentary Switch [package=ksa_sealed_tac_switch]
  Part1 = Arduino Nano (Rev3.0)
  5v = mystery part, 3 pins [chip_label=?]
  GND = mystery part, 3 pins [chip_label=?]
  U1 = mystery part, 4 pins [chip_label=?]
  ESP = mystery part, 4 pins [chip_label=?]
  Vout = female pin header, 2 pins [form="♀ (female)"]
  R3 = Resistor [tolerance=±5% resistance=220 package=THT]
  1W = female pin header, 3 pins [form="♀ (female)"]
  DHT22 = female pin header, 4 pins [form="♀ (female)"]
  R4 = Resistor [tolerance=±5% resistance=220 package=THT]
  J1 = female pin header, 15 pins [form="♀ (female)"]
  5v_2 = female pin header, 2 pins [form="♀ (female)"]
  3_3v = mystery part, 3 pins [chip_label=?]
  GND_2 = female pin header, 2 pins [form="♀ (female)"]

nets:
  N1: R1.Pin_0, Vin.pin2, S3.2, B.pin12, Part1.GND, GND.pin1, GND.pin2, GND.pin3, ESP.pin4, 1W.pin1, J1.pin2, GND_2.pin1, GND_2.pin2
  N2: R1.Pin_1, R2.Pin_0, ESP.pin1
  N3: R2.Pin_1, B.pin15, Part1.D1/TX
  N4: Vin.pin1, 5v_2.pin1, 5v_2.pin2
  N5: S3.1, S2.2
  N6: S3.3, Part1.A2, J1.pin10
  N7: S2.1, S1.2, DHT22.pin3, DHT22.pin4
  N8: S2.3, Part1.A1, J1.pin11
  N9: B.pin1, Part1.D12/MISO
  N10: B.pin2, Part1.D11/MOSI
  N11: B.pin3, Part1.D10
  N12: B.pin4, Part1.D9
  N13: B.pin5, Part1.D8, DHT22.pin2, R4.Pin_0
  N14: B.pin6, Part1.D7
  N15: B.pin7, Part1.D6
  N16: B.pin8, Part1.D5
  N17: B.pin9, Part1.D4
  N18: B.pin10, Part1.D3
  N19: B.pin11, Part1.D2, R3.Pin_1, 1W.pin2
  N20: B.pin13, Part1.RESET, J1.pin3
  N21: B.pin14, Part1.D0/RX, U1.pin4
  N22: S1.4, Part1.A0, J1.pin12
  N23: Part1.VIN, J1.pin1
  N24: Part1.5V, 5v.pin1, 5v.pin2, 5v.pin3, R3.Pin_0, 1W.pin3, DHT22.pin1, R4.Pin_1, J1.pin4
  N25: Part1.A7, J1.pin5
  N26: Part1.A6, J1.pin6
  N27: Part1.A5, J1.pin7
  N28: Part1.A4, J1.pin8
  N29: Part1.A3, J1.pin9
  N30: Part1.AREF, J1.pin13
  N31: Part1.3V3, J1.pin14
  N32: Part1.D13/SCK, J1.pin15
  N33: U1.pin1, U1.pin3, Vout.pin1, 3_3v.pin1, 3_3v.pin2, 3_3v.pin3

notes:
  CHEAPSPARK 4.2
